# Fritzing sketch Smart Home Project (saved by Fritzing 0.9.3b)
breadboards: 1

parts:
  Part1 = Arduino Uno (Rev3) - ICSP
  LCD1 = LCD screen
  U1 = POT [package=pot_alpha_rv16af-20]
  HC-SR04_Sensor_1 = HC-SR04 Ultrasonic Distance Sensor
  LED1 = RGB LED - (4 legs) [package="5 mm [THT]"]
  J1 = Piezo Speaker
  RHT1 = Humidity and Temperature Sensor RHT03
  IR1 = TSOP312.., 314.. [package=THT]
  Part2 = KY-026 Flame Sensor Module [package="Breakout board"]
  GT-511C1R1 = GT-511C1R Fingerprint Scanner

nets:
  N1: Part1.A0, Part2.A0
  N2: Part1.A3, LED1.blue_cathode
  N3: Part1.A4/SDA, LED1.green_cathode
  N4: Part1.A5/SCL, LED1.red_cathode
  VCC: Part1.5V, LCD1.LED+, U1.A, HC-SR04_Sensor_1.VCC, RHT1.Vcc, IR1.Vs, Part2.+, GT-511C1R1.Vin
  N5: Part1.D8, HC-SR04_Sensor_1.TRIG
  N6: Part1.D9_PWM, HC-SR04_Sensor_1.ECHO
  N7: Part1.D10_PWM/SS, J1.pin2
  N8: Part1.D11_PWM/MOSI, RHT1.Data-signal
  N9: Part1.D12/MISO, IR1.Data
  N10: Part1.D0/RX, LCD1.RS
  N11: Part1.D1/TX, LCD1.E
  N12: Part1.D2, GT-511C1R1.Tx
  N13: Part1.D3_PWM, GT-511C1R1.Rx
  N14: Part1.D4, LCD1.DB4
  N15: Part1.D5_PWM, LCD1.DB5
  N16: Part1.D6_PWM, LCD1.DB6
  N17: Part1.D7, LCD1.DB7
  GND: Part1.GND, LCD1.LED-, U1.E, HC-SR04_Sensor_1.GND, LED1.common_anode, J1.pin1, RHT1.GND_2, IR1.GND, Part2.G, GT-511C1R1.GND
  N18: LCD1.V0, U1.S

custom parts:
  KY-026 Flame Sensor Module: KEYES KY-026 Arduino Flame Sensor Module reacts iin the presence of fire.
  GT-511C1R Fingerprint Scanner: The GT-511C1R fingerprint scanner. The fingerprint module is produced by ADH-Tech. The GT-511C1 is based around the ARM Cortex M3 and can store 20 fingerprints.
